// Logisim project generic.circ as structural Verilog: 4 circuits, main circuit test_driver
module full_adder_4bit (
  input  a0,
  input  a1,
  input  a2,
  input  a3,
  input  b0,
  input  b1,
  input  b2,
  input  b3,
  input  carry_in,
  output s0,
  output s1,
  output s2,
  output s3,
  output carry_out
);

  wire full_adder_1_carry_out, full_adder_2_carry_out, full_adder_3_carry_out;

  full_adder full_adder_1 (.a(a0), .b(b0), .carry_in(carry_in), .sum(s0), .carry_out(full_adder_1_carry_out));
  full_adder full_adder_2 (
    .a(a1), .b(b1), .carry_in(full_adder_1_carry_out), .sum(s1), .carry_out(full_adder_2_carry_out));
  full_adder full_adder_3 (
    .a(a2), .b(b2), .carry_in(full_adder_2_carry_out), .sum(s2), .carry_out(full_adder_3_carry_out));
  full_adder full_adder_4 (.a(a3), .b(b3), .carry_in(full_adder_3_carry_out), .sum(s3), .carry_out(carry_out));
endmodule

module full_adder (
  input  a,
  input  b,
  input  carry_in,
  output sum,
  output carry_out
);

  wire and_1_out, and_2_out, xor_1_out;

  xor xor_1 (xor_1_out, a, b);
  and and_1 (and_1_out, a, b);
  and and_2 (and_2_out, xor_1_out, carry_in);
  xor xor_2 (sum, xor_1_out, carry_in);
  xor xor_3 (carry_out, and_1_out, and_2_out);
endmodule

module test_driver (
);

  wire button_1_out, button_2_out, dipswitch_1_sw1, dipswitch_1_sw2, dipswitch_1_sw3, dipswitch_1_sw4,
       dipswitch_1_sw5, dipswitch_1_sw6, dipswitch_1_sw7, dipswitch_1_sw8, dipswitch_2_sw1, dipswitch_2_sw2,
       dipswitch_2_sw3, dipswitch_2_sw4, dipswitch_2_sw5, dipswitch_2_sw6, dipswitch_2_sw7, dipswitch_2_sw8,
       full_adder_8bit_1_carry_out, full_adder_8bit_1_s0, full_adder_8bit_1_s1, full_adder_8bit_1_s2,
       full_adder_8bit_1_s3, full_adder_8bit_1_s4, full_adder_8bit_1_s5, full_adder_8bit_1_s6,
       full_adder_8bit_1_s7;

  DipSwitch dipswitch_1 (
    .sw1(dipswitch_1_sw1), .sw2(dipswitch_1_sw2), .sw3(dipswitch_1_sw3), .sw4(dipswitch_1_sw4),
    .sw5(dipswitch_1_sw5), .sw6(dipswitch_1_sw6), .sw7(dipswitch_1_sw7), .sw8(dipswitch_1_sw8));
  DipSwitch dipswitch_2 (
    .sw1(dipswitch_2_sw1), .sw2(dipswitch_2_sw2), .sw3(dipswitch_2_sw3), .sw4(dipswitch_2_sw4),
    .sw5(dipswitch_2_sw5), .sw6(dipswitch_2_sw6), .sw7(dipswitch_2_sw7), .sw8(dipswitch_2_sw8));
  Button button_1 (.out(button_1_out));
  Button button_2 (.out(button_2_out));
  full_adder_8bit full_adder_8bit_1 (
    .a0(dipswitch_1_sw1), .a1(dipswitch_1_sw2), .a2(dipswitch_1_sw3), .a3(dipswitch_1_sw4),
    .a4(dipswitch_1_sw5), .a5(dipswitch_1_sw6), .a6(dipswitch_1_sw7), .a7(dipswitch_1_sw8),
    .b0(dipswitch_2_sw1), .b1(dipswitch_2_sw2), .b2(dipswitch_2_sw3), .b3(dipswitch_2_sw4),
    .b4(dipswitch_2_sw5), .b5(dipswitch_2_sw6), .b6(dipswitch_2_sw7), .b7(dipswitch_2_sw8),
    .carry_in(button_1_out), .sub(button_2_out), .s0(full_adder_8bit_1_s0), .s1(full_adder_8bit_1_s1),
    .s2(full_adder_8bit_1_s2), .s3(full_adder_8bit_1_s3), .s4(full_adder_8bit_1_s4),
    .s5(full_adder_8bit_1_s5), .s6(full_adder_8bit_1_s6), .s7(full_adder_8bit_1_s7),
    .carry_out(full_adder_8bit_1_carry_out));
  LED led_1 (.in(full_adder_8bit_1_s0));
  LED led_2 (.in(full_adder_8bit_1_s1));
  LED led_3 (.in(full_adder_8bit_1_s2));
  LED led_4 (.in(full_adder_8bit_1_s3));
  LED led_5 (.in(full_adder_8bit_1_s4));
  LED led_6 (.in(full_adder_8bit_1_s5));
  LED led_7 (.in(full_adder_8bit_1_s6));
  LED led_8 (.in(full_adder_8bit_1_s7));
  LED carry (.in(full_adder_8bit_1_carry_out));
endmodule

module full_adder_8bit (
  input  a0,
  input  a1,
  input  a2,
  input  a3,
  input  a4,
  input  a5,
  input  a6,
  input  a7,
  input  b0,
  input  b1,
  input  b2,
  input  b3,
  input  b4,
  input  b5,
  input  b6,
  input  b7,
  input  carry_in,
  input  sub,
  output s0,
  output s1,
  output s2,
  output s3,
  output s4,
  output s5,
  output s6,
  output s7,
  output carry_out
);

  wire full_adder_4bit_1_carry_out, or_1_out, xor_1_out, xor_2_out, xor_3_out, xor_4_out, xor_5_out,
       xor_6_out, xor_7_out, xor_8_out;

  xor xor_1 (xor_1_out, b0, sub);
  xor xor_2 (xor_2_out, b1, sub);
  xor xor_3 (xor_3_out, b2, sub);
  xor xor_4 (xor_4_out, b3, sub);
  xor xor_5 (xor_5_out, b4, sub);
  xor xor_6 (xor_6_out, b5, sub);
  xor xor_7 (xor_7_out, b6, sub);
  xor xor_8 (xor_8_out, b7, sub);
  or or_1 (or_1_out, carry_in, sub);
  full_adder_4bit full_adder_4bit_1 (
    .a0(a0), .a1(a1), .a2(a2), .a3(a3), .b0(xor_1_out), .b1(xor_2_out), .b2(xor_3_out), .b3(xor_4_out),
    .carry_in(or_1_out), .s0(s0), .s1(s1), .s2(s2), .s3(s3), .carry_out(full_adder_4bit_1_carry_out));
  full_adder_4bit full_adder_4bit_2 (
    .a0(a4), .a1(a5), .a2(a6), .a3(a7), .b0(xor_5_out), .b1(xor_6_out), .b2(xor_7_out), .b3(xor_8_out),
    .carry_in(full_adder_4bit_1_carry_out), .s0(s4), .s1(s5), .s2(s6), .s3(s7), .carry_out(carry_out));
endmodule
