// Logisim project nanocomp_4bit.circ as structural Verilog: 2 circuits, main circuit nanocomp_4bit
module nanocomp_4bit (
);

  nc_alu nc_alu_1 ();  // open: a0, a1, a2, a3, b0, b1, b2, b3, c0, c1, c2, c3, clock, s0, s1, s2, s3, overflow
endmodule

module nc_alu (
  input  a0,
  input  a1,
  input  a2,
  input  a3,
  input  b0,
  input  b1,
  input  b2,
  input  b3,
  input  c0,
  input  c1,
  input  c2,
  input  c3,
  input  clock,
  output s0,
  output s1,
  output s2,
  output s3,
  output overflow
);

  wire decoder_1_out0, decoder_1_out1, decoder_1_out2, decoder_1_out3, decoder_1_out4, decoder_1_out5,
       decoder_1_out6, decoder_1_out7, decoder_1_out8, decoder_1_out9, decoder_1_out10, decoder_1_out11,
       decoder_1_out12, decoder_1_out13, decoder_1_out14, decoder_1_out15;
  wire [3:0] adder_1_out, and_1_out, buffer_1_out, buffer_2_out, multiplexer_1_out, not_1_out, or_1_out,
       shifter_1_out, shifter_2_out, xor_1_out, xor_5_out;
  wire [3:3] comparator_1_eq, comparator_1_gt, comparator_1_lt, comparator_2_eq, comparator_2_gt,
       comparator_2_lt;

  Decoder #(.select(4)) decoder_1 (
    .out0(decoder_1_out0), .out1(decoder_1_out1), .out2(decoder_1_out2), .out3(decoder_1_out3),
    .out4(decoder_1_out4), .out5(decoder_1_out5), .out6(decoder_1_out6), .out7(decoder_1_out7),
    .out8(decoder_1_out8), .out9(decoder_1_out9), .out10(decoder_1_out10), .out11(decoder_1_out11),
    .out12(decoder_1_out12), .out13(decoder_1_out13), .out14(decoder_1_out14), .out15(decoder_1_out15),
    .sel({c3, c2, c1, c0}));  // open: en
  xor xor_1 (xor_1_out[0], b0, decoder_1_out11);
  xor xor_2 (xor_1_out[1], b1, decoder_1_out11);
  xor xor_3 (xor_1_out[2], b2, decoder_1_out11);
  xor xor_4 (xor_1_out[3], b3, decoder_1_out11);
  LED opbuf (.in(decoder_1_out0));
  LED opor (.in(decoder_1_out1));
  LED opand (.in(decoder_1_out2));
  LED opnot (.in(decoder_1_out3));
  LED opxor (.in(decoder_1_out4));
  LED gt2c (.in(decoder_1_out5));
  LED eq2c (.in(decoder_1_out6));
  LED lt2c (.in(decoder_1_out7));
  LED gtunsig (.in(decoder_1_out8));
  LED equnsig (.in(decoder_1_out9));
  LED opadd (.in(decoder_1_out10));
  LED opsub (.in(decoder_1_out11));
  LED ltunsig (.in(decoder_1_out12));
  LED lshift (.in(decoder_1_out13));
  LED rshift (.in(decoder_1_out14));
  LED bufb (.in(decoder_1_out15));
  assign buffer_1_out = {a3, a2, a1, a0};  // Buffer buffer_1, 4 bits wide
  assign buffer_2_out = {b3, b2, b1, b0};  // Buffer buffer_2, 4 bits wide
  Adder #(.width(4)) adder_1 (
    .a({a3, a2, a1, a0}), .b(xor_1_out), .out(adder_1_out), .cin(decoder_1_out11), .cout(overflow));
  assign or_1_out = {a3, a2, a1, a0} | {b3, b2, b1, b0};  // OR_Gate or_1, 4 bits wide
  assign and_1_out = {a3, a2, a1, a0} & {b3, b2, b1, b0};  // AND_Gate and_1, 4 bits wide
  assign not_1_out = ~{a3, a2, a1, a0};  // NOT_Gate not_1, 4 bits wide
  Comparator #(.width(4), .mode("unsigned")) comparator_1 (
    .a({a3, a2, a1, a0}), .b({b3, b2, b1, b0}), .gt(comparator_1_gt[3]), .eq(comparator_1_eq[3]),
    .lt(comparator_1_lt[3]));
  Comparator #(.width(4)) comparator_2 (
    .a({a3, a2, a1, a0}), .b({b3, b2, b1, b0}), .gt(comparator_2_gt[3]), .eq(comparator_2_eq[3]),
    .lt(comparator_2_lt[3]));
  Shifter #(.width(4)) shifter_1 (.in({a3, a2, a1, a0}), .\dist ({b1, b0}), .out(shifter_1_out));
  Shifter #(.width(4), .shift("lr")) shifter_2 (.in({a3, a2, a1, a0}), .\dist ({b1, b0}), .out(shifter_2_out));
  assign xor_5_out = {a3, a2, a1, a0} ^ {b3, b2, b1, b0};  // XOR_Gate xor_5, 4 bits wide
  Multiplexer #(.select(4), .width(4), .enable("false")) multiplexer_1 (
    .in0(buffer_1_out), .in1(or_1_out), .in2(and_1_out), .in3(not_1_out), .in4(xor_5_out),
    .in5({4{comparator_1_gt[3]}}), .in6({4{comparator_1_eq[3]}}), .in7({4{comparator_1_lt[3]}}),
    .in8({4{comparator_2_gt[3]}}), .in9({4{comparator_2_eq[3]}}), .in10(adder_1_out), .in11(adder_1_out),
    .in12({4{comparator_2_lt[3]}}), .in13(shifter_1_out), .in14(shifter_2_out), .in15(buffer_2_out),
    .out(multiplexer_1_out), .sel({c3, c2, c1, c0}));
  D_Flip_Flop d_ff_1 (.D(multiplexer_1_out[0]), .clk(clock), .Q(s0));  // open: Qn, preset, reset
  D_Flip_Flop d_ff_2 (.D(multiplexer_1_out[1]), .clk(clock), .Q(s1));  // open: Qn, preset, reset
  D_Flip_Flop d_ff_3 (.D(multiplexer_1_out[2]), .clk(clock), .Q(s2));  // open: Qn, preset, reset
  D_Flip_Flop d_ff_4 (.D(multiplexer_1_out[3]), .clk(clock), .Q(s3));  // open: Qn, preset, reset

  // Notes on the sheet:
  //   ALU Program Codes
endmodule
